// Logisim project control-logic.circ as structural Verilog: 1 circuit, main circuit control_logic
module control_logic (
  input  [31:0] Instruction,
  input  BrEq,
  input  BrLt,
  output PCSel,
  output RegWEn,
  output [2:0] ImmSel,
  output BrUn,
  output ASel,
  output BSel,
  output [3:0] ALUSel,
  output MemRW,
  output [1:0] WBSel
);

  wire and_1_out, and_2_out, and_3_out, and_4_out, and_5_out, and_6_out, and_7_out, and_8_out, and_9_out,
       and_10_out, and_11_out, and_12_out, and_26_out, and_27_out, and_28_out, and_29_out, and_30_out,
       and_31_out, and_33_out, and_38_out, and_39_out, comparator_10_eq, comparator_11_eq, comparator_12_eq,
       comparator_13_eq, comparator_14_eq, comparator_15_eq, comparator_16_eq, comparator_17_eq,
       comparator_18_eq, comparator_19_eq, comparator_20_eq, comparator_21_eq, comparator_22_eq,
       comparator_23_eq, comparator_24_eq, comparator_25_eq, comparator_26_eq, comparator_27_eq,
       comparator_28_eq, comparator_29_eq, comparator_30_eq, comparator_31_eq, comparator_32_eq,
       comparator_33_eq, comparator_34_eq, comparator_35_eq, comparator_36_eq, comparator_37_eq,
       comparator_38_eq, comparator_39_eq, comparator_40_eq, comparator_41_eq, comparator_42_eq,
       comparator_43_eq, comparator_44_eq, comparator_45_eq, comparator_46_eq, comparator_47_eq,
       comparator_48_eq, comparator_49_eq, comparator_50_eq, comparator_51_eq, comparator_52_eq,
       comparator_53_eq, comparator_54_eq, comparator_55_eq, comparator_56_eq, comparator_57_eq, is_0, is_1,
       is_2, is_3, is_4, is_5, is_6, is_7, is_8, is_9, is_10, is_11, is_12, is_13, is_14, is_15, is_16,
       is_17, is_18, is_19, is_20, is_21, is_22, is_23, is_24, is_25, is_26, is_27, is_28, is_29, is_30,
       is_31, is_32, is_33, is_34, is_35, is_B, is_I_1, is_I_2, is_I_3, is_R, is_S, not_1_out, not_2_out,
       not_3_out, or_1_out, or_2_out;
  wire [5:0] rom_input;
  wire [15:14] rom_1_data;

  Comparator #(.width(5)) comparator_1 (.a(Instruction[6:2]), .b(5'b01100), .eq(is_R));  // open: gt, lt
  Comparator #(.width(5)) comparator_2 (.a(Instruction[6:2]), .b({5{1'b0}}), .eq(is_I_1));  // open: gt, lt
  Comparator #(.width(5)) comparator_3 (.a(Instruction[6:2]), .b(5'b00100), .eq(is_I_2));  // open: gt, lt
  Comparator #(.width(5)) comparator_4 (.a(Instruction[6:2]), .b(5'b01000), .eq(is_S));  // open: gt, lt
  Comparator #(.width(5)) comparator_5 (.a(Instruction[6:2]), .b(5'b11000), .eq(is_B));  // open: gt, lt
  Comparator #(.width(5)) comparator_6 (.a(Instruction[6:2]), .b(5'b00011), .eq(is_32));  // open: gt, lt
  Comparator #(.width(5)) comparator_7 (.a(Instruction[6:2]), .b(5'b01101), .eq(is_33));  // open: gt, lt
  Comparator #(.width(5)) comparator_8 (.a(Instruction[6:2]), .b(5'b11011), .eq(is_34));  // open: gt, lt
  Comparator #(.width(5)) comparator_9 (.a(Instruction[6:2]), .b(5'b11001), .eq(is_I_3));  // open: gt, lt
  ROM #(.addrWidth(6), .dataWidth(16)) rom_1 (
    .addr(rom_input), .data({rom_1_data, WBSel, MemRW, ALUSel, BSel, ASel, BrUn, ImmSel, RegWEn}));
  Comparator #(.width(3)) comparator_10 (.a(Instruction[14:12]), .b(3'b000), .eq(comparator_10_eq));  // open: gt, lt
  Comparator #(.width(3)) comparator_11 (.a(Instruction[14:12]), .b(3'b000), .eq(comparator_11_eq));  // open: gt, lt
  Comparator #(.width(3)) comparator_12 (.a(Instruction[14:12]), .b(3'b000), .eq(comparator_12_eq));  // open: gt, lt
  Comparator #(.width(3)) comparator_13 (.a(Instruction[14:12]), .b(3'b001), .eq(comparator_13_eq));  // open: gt, lt
  Comparator #(.width(3)) comparator_14 (.a(Instruction[14:12]), .b(3'b001), .eq(comparator_14_eq));  // open: gt, lt
  Comparator #(.width(3)) comparator_15 (.a(Instruction[14:12]), .b(3'b011), .eq(comparator_15_eq));  // open: gt, lt
  Comparator #(.width(3)) comparator_16 (.a(Instruction[14:12]), .b(3'b010), .eq(comparator_16_eq));  // open: gt, lt
  Comparator #(.width(3)) comparator_17 (.a(Instruction[14:12]), .b(3'b100), .eq(comparator_17_eq));  // open: gt, lt
  Comparator #(.width(3)) comparator_18 (.a(Instruction[14:12]), .b(3'b101), .eq(comparator_18_eq));  // open: gt, lt
  Comparator #(.width(3)) comparator_19 (.a(Instruction[14:12]), .b(3'b101), .eq(comparator_19_eq));  // open: gt, lt
  Comparator #(.width(3)) comparator_20 (.a(Instruction[14:12]), .b(3'b110), .eq(comparator_20_eq));  // open: gt, lt
  Comparator #(.width(3)) comparator_21 (.a(Instruction[14:12]), .b(3'b111), .eq(comparator_21_eq));  // open: gt, lt
  Comparator #(.width(3)) comparator_22 (.a(Instruction[14:12]), .b(3'b000), .eq(comparator_22_eq));  // open: gt, lt
  and and_1 (and_1_out, is_R, comparator_10_eq);
  Comparator #(.width(7)) comparator_23 (.a(Instruction[31:25]), .b({7{1'b0}}), .eq(comparator_23_eq));  // open: gt, lt
  and and_2 (and_2_out, is_R, comparator_11_eq);
  Comparator #(.width(7)) comparator_24 (
    .a(Instruction[31:25]), .b(7'b0000001), .eq(comparator_24_eq));  // open: gt, lt
  and and_3 (and_3_out, is_R, comparator_12_eq);
  Comparator #(.width(7)) comparator_25 (
    .a(Instruction[31:25]), .b(7'b0100000), .eq(comparator_25_eq));  // open: gt, lt
  and and_4 (and_4_out, is_R, comparator_13_eq);
  Comparator #(.width(7)) comparator_26 (.a(Instruction[31:25]), .b({7{1'b0}}), .eq(comparator_26_eq));  // open: gt, lt
  and and_5 (and_5_out, is_R, comparator_14_eq);
  Comparator #(.width(7)) comparator_27 (
    .a(Instruction[31:25]), .b(7'b0000001), .eq(comparator_27_eq));  // open: gt, lt
  and and_6 (and_6_out, is_R, comparator_16_eq);
  Comparator #(.width(7)) comparator_28 (.a(Instruction[31:25]), .b({7{1'b0}}), .eq(comparator_28_eq));  // open: gt, lt
  and and_7 (and_7_out, is_R, comparator_15_eq);
  Comparator #(.width(7)) comparator_29 (
    .a(Instruction[31:25]), .b(7'b0000001), .eq(comparator_29_eq));  // open: gt, lt
  and and_8 (and_8_out, is_R, comparator_17_eq);
  Comparator #(.width(7)) comparator_30 (.a(Instruction[31:25]), .b({7{1'b0}}), .eq(comparator_30_eq));  // open: gt, lt
  and and_9 (and_9_out, is_R, comparator_18_eq);
  Comparator #(.width(7)) comparator_31 (.a(Instruction[31:25]), .b({7{1'b0}}), .eq(comparator_31_eq));  // open: gt, lt
  and and_10 (and_10_out, is_R, comparator_19_eq);
  Comparator #(.width(7)) comparator_32 (
    .a(Instruction[31:25]), .b(7'b0100000), .eq(comparator_32_eq));  // open: gt, lt
  and and_11 (and_11_out, is_R, comparator_20_eq);
  Comparator #(.width(7)) comparator_33 (.a(Instruction[31:25]), .b({7{1'b0}}), .eq(comparator_33_eq));  // open: gt, lt
  and and_12 (and_12_out, is_R, comparator_21_eq);
  Comparator #(.width(7)) comparator_34 (.a(Instruction[31:25]), .b({7{1'b0}}), .eq(comparator_34_eq));  // open: gt, lt
  and and_13 (is_12, is_I_1, comparator_22_eq);
  and and_14 (is_0, and_1_out, comparator_23_eq);
  and and_15 (is_1, and_2_out, comparator_24_eq);
  and and_16 (is_2, and_3_out, comparator_25_eq);
  and and_17 (is_3, and_4_out, comparator_26_eq);
  and and_18 (is_4, and_5_out, comparator_27_eq);
  and and_19 (is_5, and_7_out, comparator_29_eq);
  and and_20 (is_6, and_6_out, comparator_28_eq);
  and and_21 (is_7, and_8_out, comparator_30_eq);
  and and_22 (is_8, and_9_out, comparator_31_eq);
  and and_23 (is_9, and_10_out, comparator_32_eq);
  and and_24 (is_10, and_11_out, comparator_33_eq);
  and and_25 (is_11, and_12_out, comparator_34_eq);
  not not_1 (not_1_out, BrEq);
  and and_26 (and_26_out, is_26, BrEq);
  and and_27 (and_27_out, is_27, not_1_out);
  and and_28 (and_28_out, is_28, BrLt);
  and and_29 (and_29_out, is_30, BrLt);
  not not_2 (not_2_out, BrLt);
  not not_3 (not_3_out, BrLt);
  and and_30 (and_30_out, is_29, not_2_out);
  and and_31 (and_31_out, is_31, not_3_out);
  Comparator #(.width(3)) comparator_35 (.a(Instruction[14:12]), .b(3'b001), .eq(comparator_35_eq));  // open: gt, lt
  Comparator #(.width(3)) comparator_36 (.a(Instruction[14:12]), .b(3'b010), .eq(comparator_36_eq));  // open: gt, lt
  Comparator #(.width(3)) comparator_37 (.a(Instruction[14:12]), .b(3'b000), .eq(comparator_37_eq));  // open: gt, lt
  Comparator #(.width(3)) comparator_38 (.a(Instruction[14:12]), .b(3'b001), .eq(comparator_38_eq));  // open: gt, lt
  Comparator #(.width(3)) comparator_39 (.a(Instruction[14:12]), .b(3'b010), .eq(comparator_39_eq));  // open: gt, lt
  Comparator #(.width(3)) comparator_40 (.a(Instruction[14:12]), .b(3'b100), .eq(comparator_40_eq));  // open: gt, lt
  Comparator #(.width(3)) comparator_41 (.a(Instruction[14:12]), .b(3'b101), .eq(comparator_41_eq));  // open: gt, lt
  Comparator #(.width(3)) comparator_42 (.a(Instruction[14:12]), .b(3'b101), .eq(comparator_42_eq));  // open: gt, lt
  Comparator #(.width(3)) comparator_43 (.a(Instruction[14:12]), .b(3'b110), .eq(comparator_43_eq));  // open: gt, lt
  Comparator #(.width(3)) comparator_44 (.a(Instruction[14:12]), .b(3'b111), .eq(comparator_44_eq));  // open: gt, lt
  Comparator #(.width(3)) comparator_45 (.a(Instruction[14:12]), .b(3'b000), .eq(comparator_45_eq));  // open: gt, lt
  Comparator #(.width(3)) comparator_46 (.a(Instruction[14:12]), .b(3'b001), .eq(comparator_46_eq));  // open: gt, lt
  Comparator #(.width(3)) comparator_47 (.a(Instruction[14:12]), .b(3'b010), .eq(comparator_47_eq));  // open: gt, lt
  Comparator #(.width(3)) comparator_48 (.a(Instruction[14:12]), .b(3'b000), .eq(comparator_48_eq));  // open: gt, lt
  Comparator #(.width(3)) comparator_49 (.a(Instruction[14:12]), .b(3'b001), .eq(comparator_49_eq));  // open: gt, lt
  Comparator #(.width(3)) comparator_50 (.a(Instruction[14:12]), .b(3'b100), .eq(comparator_50_eq));  // open: gt, lt
  Comparator #(.width(3)) comparator_51 (.a(Instruction[14:12]), .b(3'b101), .eq(comparator_51_eq));  // open: gt, lt
  Comparator #(.width(3)) comparator_52 (.a(Instruction[14:12]), .b(3'b110), .eq(comparator_52_eq));  // open: gt, lt
  Comparator #(.width(3)) comparator_53 (.a(Instruction[14:12]), .b(3'b111), .eq(comparator_53_eq));  // open: gt, lt
  Comparator #(.width(3)) comparator_54 (.a(Instruction[14:12]), .b(3'b000), .eq(comparator_54_eq));  // open: gt, lt
  and and_32 (is_13, is_I_1, comparator_35_eq);
  and and_33 (and_33_out, is_I_2, comparator_38_eq);
  Comparator #(.width(7)) comparator_55 (.a(Instruction[31:25]), .b({7{1'b0}}), .eq(comparator_55_eq));  // open: gt, lt
  or or_1 (or_1_out, and_26_out, and_27_out, and_28_out, and_29_out, and_30_out, and_31_out);
  and and_34 (is_14, is_I_1, comparator_36_eq);
  and and_35 (is_15, is_I_2, comparator_37_eq);
  and and_36 (is_17, is_I_2, comparator_39_eq);
  and and_37 (is_18, is_I_2, comparator_40_eq);
  and and_38 (and_38_out, is_I_2, comparator_41_eq);
  Comparator #(.width(7)) comparator_56 (.a(Instruction[31:25]), .b({7{1'b0}}), .eq(comparator_56_eq));  // open: gt, lt
  and and_39 (and_39_out, is_I_2, comparator_42_eq);
  Comparator #(.width(7)) comparator_57 (
    .a(Instruction[31:25]), .b(7'b0100000), .eq(comparator_57_eq));  // open: gt, lt
  and and_40 (is_21, is_I_2, comparator_43_eq);
  and and_41 (is_22, is_I_2, comparator_44_eq);
  and and_42 (is_23, is_S, comparator_45_eq);
  and and_43 (is_24, is_S, comparator_46_eq);
  and and_44 (is_25, is_S, comparator_47_eq);
  and and_45 (is_26, is_B, comparator_48_eq);
  and and_46 (is_27, is_B, comparator_49_eq);
  and and_47 (is_28, is_B, comparator_50_eq);
  and and_48 (is_29, is_B, comparator_51_eq);
  and and_49 (is_30, is_B, comparator_52_eq);
  and and_50 (is_31, is_B, comparator_53_eq);
  and and_51 (is_35, is_I_3, comparator_54_eq);
  or or_2 (or_2_out, is_34, is_35);
  and and_52 (is_16, and_33_out, comparator_55_eq);
  and and_53 (is_19, and_38_out, comparator_56_eq);
  and and_54 (is_20, and_39_out, comparator_57_eq);
  or or_3 (PCSel, or_2_out, or_1_out);
  Priority_Encoder #(.select_enc(6)) priority_encoder_1 (
    .in0(is_0), .in1(is_1), .in2(is_2), .in3(is_3), .in4(is_4), .in5(is_5), .in6(is_6), .in7(is_7),
    .in8(is_8), .in9(is_9), .in10(is_10), .in11(is_11), .in12(is_12), .in13(is_13), .in14(is_14),
    .in15(is_15), .in16(is_16), .in17(is_17), .in18(is_18), .in19(is_19), .in20(is_20), .in21(is_21),
    .in22(is_22), .in23(is_23), .in24(is_24), .in25(is_25), .in26(is_26), .in27(is_27), .in28(is_28),
    .in29(is_29), .in30(is_30), .in31(is_31), .in32(is_32), .in33(is_33), .in34(is_34), .in35(is_35),
    .out(rom_input));  // open: in36, in37, in38, in39, in40, in41, in42, in43, in44, in45, in46, in47, in48, in49, in50, in51, in52, in53, in54, in55, in56, in57, in58, in59, in60, in61, in62, in63, gs, en_out, en_in

  // Other names for the same wires on the sheet: opcode[4:0] = Instruction[6:2]; funct3[2:0] = Instruction[14:12];
  //   funct7[6:0] = Instruction[31:25]; is_J = is_34; is_U_1 = is_32; is_U_2 = is_33

  // Notes on the sheet:
  //   INPUTS to your circuit
  //   contents of rom_1 (hex, n*v repeats v):
  //   100f 140f 160f 108f 148f 158f 110f 120f 128f 168f 130f 138f 41 41 41 1041 10c1 1141 1241 12c1 16c1
  //   1341 13c1 842 842 842 4*64 74 74 1067 17c7 2069 2041
  //   ROM FOR CONTROL LOGIC
  //   DON'T CHANGE THE LOCATIONS OF THE INPUTS AND OUTPUTS!
  //   This is only if you choose to do the ROM option
  //   OUTPUT from your circuit
endmodule
