// Logisim project regfile.circ as structural Verilog: 1 circuit, main circuit regfile
module regfile (
  input  [4:0] ReadIndex1,
  input  [4:0] ReadIndex2,
  input  [4:0] WriteIndex,
  input  [31:0] WriteData,
  input  RegWEn,
  input  clk,
  output [31:0] ra,
  output [31:0] sp,
  output [31:0] t0,
  output [31:0] t1,
  output [31:0] t2,
  output [31:0] s0,
  output [31:0] s1,
  output [31:0] a0,
  output [31:0] ReadData1,
  output [31:0] ReadData2
);

  wire REn0, REn1, REn2, REn3, REn4, REn5, REn6, REn7, REn8, REn9, REn10, REn11, REn12, REn13, REn14, REn15,
       REn16, REn17, REn18, REn19, REn20, REn21, REn22, REn23, REn24, REn25, REn26, REn27, REn28, REn29,
       REn30, REn31;
  wire [31:0] a1, a2, a3, a4, a5, a6, a7, gp, s2, s3, s4, s5, s6, s7, s8, s9, s10, s11, t3, t4, t5, t6, tp,
       zero;

  Register #(.width(32)) x0 (.D(WriteData), .en(REn0), .clk(clk), .Q(zero));  // open: clr
  Register #(.width(32)) x4 (.D(WriteData), .en(REn4), .clk(clk), .Q(tp));  // open: clr
  Register #(.width(32)) x8 (.D(WriteData), .en(REn8), .clk(clk), .Q(s0));  // open: clr
  Register #(.width(32)) x12 (.D(WriteData), .en(REn12), .clk(clk), .Q(a2));  // open: clr
  Register #(.width(32)) x16 (.D(WriteData), .en(REn16), .clk(clk), .Q(a6));  // open: clr
  Register #(.width(32)) x20 (.D(WriteData), .en(REn20), .clk(clk), .Q(s4));  // open: clr
  Register #(.width(32)) x24 (.D(WriteData), .en(REn24), .clk(clk), .Q(s8));  // open: clr
  Register #(.width(32)) x28 (.D(WriteData), .en(REn28), .clk(clk), .Q(t3));  // open: clr
  Register #(.width(32)) x1 (.D(WriteData), .en(REn1), .clk(clk), .Q(ra));  // open: clr
  Register #(.width(32)) x5 (.D(WriteData), .en(REn5), .clk(clk), .Q(t0));  // open: clr
  Register #(.width(32)) x9 (.D(WriteData), .en(REn9), .clk(clk), .Q(s1));  // open: clr
  Register #(.width(32)) x13 (.D(WriteData), .en(REn13), .clk(clk), .Q(a3));  // open: clr
  Register #(.width(32)) x17 (.D(WriteData), .en(REn17), .clk(clk), .Q(a7));  // open: clr
  Register #(.width(32)) x21 (.D(WriteData), .en(REn21), .clk(clk), .Q(s5));  // open: clr
  Register #(.width(32)) x25 (.D(WriteData), .en(REn25), .clk(clk), .Q(s9));  // open: clr
  Register #(.width(32)) x29 (.D(WriteData), .en(REn29), .clk(clk), .Q(t4));  // open: clr
  Multiplexer #(.select(5), .width(32)) multiplexer_1 (
    .in0(zero), .in1(ra), .in2(sp), .in3(gp), .in4(tp), .in5(t0), .in6(t1), .in7(t2), .in8(s0), .in9(s1),
    .in10(a0), .in11(a1), .in12(a2), .in13(a3), .in14(a4), .in15(a5), .in16(a6), .in17(a7), .in18(s2),
    .in19(s3), .in20(s4), .in21(s5), .in22(s6), .in23(s7), .in24(s8), .in25(s9), .in26(s10), .in27(s11),
    .in28(t3), .in29(t4), .in30(t5), .in31(t6), .out(ReadData1), .sel(ReadIndex1));
  Register #(.width(32)) x2 (.D(WriteData), .en(REn2), .clk(clk), .Q(sp));  // open: clr
  Register #(.width(32)) x6 (.D(WriteData), .en(REn6), .clk(clk), .Q(t1));  // open: clr
  Register #(.width(32)) x10 (.D(WriteData), .en(REn10), .clk(clk), .Q(a0));  // open: clr
  Register #(.width(32)) x14 (.D(WriteData), .en(REn14), .clk(clk), .Q(a4));  // open: clr
  Register #(.width(32)) x18 (.D(WriteData), .en(REn18), .clk(clk), .Q(s2));  // open: clr
  Register #(.width(32)) x22 (.D(WriteData), .en(REn22), .clk(clk), .Q(s6));  // open: clr
  Register #(.width(32)) x26 (.D(WriteData), .en(REn26), .clk(clk), .Q(s10));  // open: clr
  Register #(.width(32)) x30 (.D(WriteData), .en(REn30), .clk(clk), .Q(t5));  // open: clr
  Register #(.width(32)) x3 (.D(WriteData), .en(REn3), .clk(clk), .Q(gp));  // open: clr
  Register #(.width(32)) x7 (.D(WriteData), .en(REn7), .clk(clk), .Q(t2));  // open: clr
  Register #(.width(32)) x11 (.D(WriteData), .en(REn11), .clk(clk), .Q(a1));  // open: clr
  Register #(.width(32)) x15 (.D(WriteData), .en(REn15), .clk(clk), .Q(a5));  // open: clr
  Register #(.width(32)) x19 (.D(WriteData), .en(REn19), .clk(clk), .Q(s3));  // open: clr
  Register #(.width(32)) x23 (.D(WriteData), .en(REn23), .clk(clk), .Q(s7));  // open: clr
  Register #(.width(32)) x27 (.D(WriteData), .en(REn27), .clk(clk), .Q(s11));  // open: clr
  Register #(.width(32)) x31 (.D(WriteData), .en(REn31), .clk(clk), .Q(t6));  // open: clr
  Multiplexer #(.select(5), .width(32)) multiplexer_2 (
    .in0(zero), .in1(ra), .in2(sp), .in3(gp), .in4(tp), .in5(t0), .in6(t1), .in7(t2), .in8(s0), .in9(s1),
    .in10(a0), .in11(a1), .in12(a2), .in13(a3), .in14(a4), .in15(a5), .in16(a6), .in17(a7), .in18(s2),
    .in19(s3), .in20(s4), .in21(s5), .in22(s6), .in23(s7), .in24(s8), .in25(s9), .in26(s10), .in27(s11),
    .in28(t3), .in29(t4), .in30(t5), .in31(t6), .out(ReadData2), .sel(ReadIndex2));
  Multiplexer #(.select(5)) multiplexer_3 (
    .in0(REn0), .in1(REn1), .in2(REn2), .in3(REn3), .in4(REn4), .in5(REn5), .in6(REn6), .in7(REn7),
    .in8(REn8), .in9(REn9), .in10(REn10), .in11(REn11), .in12(REn12), .in13(REn13), .in14(REn14),
    .in15(REn15), .in16(REn16), .in17(REn17), .in18(REn18), .in19(REn19), .in20(REn20), .in21(REn21),
    .in22(REn22), .in23(REn23), .in24(REn24), .in25(REn25), .in26(REn26), .in27(REn27), .in28(REn28),
    .in29(REn29), .in30(REn30), .in31(REn31), .out(RegWEn), .sel(WriteIndex));

  // Notes on the sheet:
  //   INPUTS to your circuit
  //   DON'T CHANGE THE LOCATIONS OF THE INPUTS AND OUTPUTS!
  //   These are DEBUG/TEST outputs from your circuit.
  //   OUTPUTS from your circuit
endmodule
