// Logisim project m05_sh_mask_and_truncation.circ as structural Verilog: 1 circuit, main circuit run_main
module run_main (
  output [31:0] ra,
  output [31:0] sp,
  output [31:0] t0,
  output [31:0] t1,
  output [31:0] t2,
  output [31:0] s0,
  output [31:0] s1,
  output [31:0] a0,
  output [31:0] RequestedAddress,
  output [31:0] RequestedInstruction,
  output [15:0] TimeStep,
  output halt
);

  wire clk;

  Clock clock_1 (.out(clk));
  // Probe on RequestedAddress
  // cpu_harness cpu_harness_1: pin names not known; wires that end beside it: RequestedInstruction, clk, RequestedAddress, ra, sp, t0, t1, t2, s0, s1, a0
  ROM #(.addrWidth(14), .dataWidth(32)) rom_1 (.addr(RequestedAddress[15:2]), .data(RequestedInstruction));
  // Probe on RequestedInstruction
  Counter #(.max('hffff), .width(16)) counter_1 (.clk(clk), .Q(TimeStep));  // open: clr, load, up, count, D, carry
  Comparator #(.width(16)) comparator_1 (.a(TimeStep), .b(16'h8b), .eq(halt));  // open: gt, lt

  // Other names for the same wires on the sheet: Instruction[31:0] = RequestedInstruction;
  //   ProgramCounter[31:0] = RequestedAddress

  // Notes on the sheet:
  //   contents of rom_1 (hex, n*v repeats v):
  //   40000293 15500313 b31313 4ce30313 b31313 78830313 fe62ae23 26600313 b31313 55730313 b31313 3cc30313
  //   62a223 4400313 b31313 44630313 b31313 34430313 62a023 28600313 b31313 64030313 b31313 629023 2a383
  //   ffc2a403 42a483 29503 4400313 b31313 44630313 b31313 34430313 62a023 28600313 b31313 64f30313 b31313
  //   7ff30313 629023 2a383 ffc2a403 42a483 29503 4400313 b31313 44630313 b31313 34430313 62a023 28600313
  //   b31313 65030313 b31313 629023 2a383 ffc2a403 42a483 29503 4400313 b31313 44630313 b31313 34430313
  //   62a023 28600313 b31313 65f30313 b31313 7ff30313 629023 2a383 ffc2a403 42a483 29503 4400313 b31313
  //   44630313 b31313 34430313 62a023 28600313 b31313 64030313 b31313 629123 2a383 ffc2a403 42a483 229503
  //   4400313 b31313 44630313 b31313 34430313 62a023 28600313 b31313 64f30313 b31313 7ff30313 629123 2a383
  //   ffc2a403 42a483 229503 4400313 b31313 44630313 b31313 34430313 62a023 28600313 b31313 65030313
  //   b31313 629123 2a383 ffc2a403 42a483 229503 4400313 b31313 44630313 b31313 34430313 62a023 28600313
  //   b31313 65f30313 b31313 7ff30313 629123 2a383 ffc2a403 42a483 229503
  //   Instruction Memory
  //   Halts Execution After Constant # of Clock Cycles
  //   Constant
endmodule
