// Logisim project m06_overlapping_stores.circ as structural Verilog: 1 circuit, main circuit run_main
module run_main (
  output [31:0] ra,
  output [31:0] sp,
  output [31:0] t0,
  output [31:0] t1,
  output [31:0] t2,
  output [31:0] s0,
  output [31:0] s1,
  output [31:0] a0,
  output [31:0] RequestedAddress,
  output [31:0] RequestedInstruction,
  output [15:0] TimeStep,
  output halt
);

  wire clk;

  Clock clock_1 (.out(clk));
  // Probe on RequestedAddress
  // cpu_harness cpu_harness_1: pin names not known; wires that end beside it: RequestedInstruction, clk, RequestedAddress, ra, sp, t0, t1, t2, s0, s1, a0
  ROM #(.addrWidth(14), .dataWidth(32)) rom_1 (.addr(RequestedAddress[15:2]), .data(RequestedInstruction));
  // Probe on RequestedInstruction
  Counter #(.max('hffff), .width(16)) counter_1 (.clk(clk), .Q(TimeStep));  // open: clr, load, up, count, D, carry
  Comparator #(.width(16)) comparator_1 (.a(TimeStep), .b(16'h4d), .eq(halt));  // open: gt, lt

  // Other names for the same wires on the sheet: Instruction[31:0] = RequestedInstruction;
  //   ProgramCounter[31:0] = RequestedAddress

  // Notes on the sheet:
  //   contents of rom_1 (hex, n*v repeats v):
  //   40000293 15500313 b31313 4ce30313 b31313 78830313 fe62ae23 26600313 b31313 55730313 b31313 3cc30313
  //   62a223 4400313 b31313 44630313 b31313 34430313 62a023 aa00313 6280a3 2a383 ffc2a403 42a483 313
  //   b31313 1730313 b31313 6ef30313 629123 2a383 ffc2a403 42a483 313 6281a3 2a383 ffc2a403 42a483 313
  //   b31313 1030313 b31313 130313 629023 2a383 ffc2a403 42a483 7f00313 628123 2a383 ffc2a403 42a483
  //   37a00313 b31313 5b730313 b31313 6ef30313 62a023 2a383 ffc2a403 42a483 1200313 628023 2a383 ffc2a403
  //   42a483 313 629123 2a383 ffc2a403 42a483 28503 128583 228603 328683
  //   Instruction Memory
  //   Halts Execution After Constant # of Clock Cycles
  //   Constant
endmodule
