// Logisim project m07_load_immediate_bits.circ as structural Verilog: 1 circuit, main circuit run_main
module run_main (
  output [31:0] ra,
  output [31:0] sp,
  output [31:0] t0,
  output [31:0] t1,
  output [31:0] t2,
  output [31:0] s0,
  output [31:0] s1,
  output [31:0] a0,
  output [31:0] RequestedAddress,
  output [31:0] RequestedInstruction,
  output [15:0] TimeStep,
  output halt
);

  wire clk;

  Clock clock_1 (.out(clk));
  // Probe on RequestedAddress
  // cpu_harness cpu_harness_1: pin names not known; wires that end beside it: RequestedInstruction, clk, RequestedAddress, ra, sp, t0, t1, t2, s0, s1, a0
  ROM #(.addrWidth(14), .dataWidth(32)) rom_1 (.addr(RequestedAddress[15:2]), .data(RequestedInstruction));
  // Probe on RequestedInstruction
  Counter #(.max('hffff), .width(16)) counter_1 (.clk(clk), .Q(TimeStep));  // open: clr, load, up, count, D, carry
  Comparator #(.width(16)) comparator_1 (.a(TimeStep), .b(16'haa), .eq(halt));  // open: gt, lt

  // Other names for the same wires on the sheet: Instruction[31:0] = RequestedInstruction;
  //   ProgramCounter[31:0] = RequestedAddress

  // Notes on the sheet:
  //   contents of rom_1 (hex, n*v repeats v):
  //   293 b29293 228293 b29293 20700313 b31313 7d030313 b31313 7f30313 62a023 413 b41413 240413 b41413
  //   40383 41503 42583 413 b41413 140413 b41413 7ff40413 140383 141503 142583 413 b41413 140413 b41413
  //   7fe40413 240383 241503 242583 413 b41413 140413 b41413 7fc40413 440383 441503 442583 413 b41413
  //   140413 b41413 7f840413 840383 841503 842583 413 b41413 140413 b41413 7f040413 1040383 1041503
  //   1042583 413 b41413 140413 b41413 7e140413 1f40383 1f41503 1f42583 413 b41413 140413 b41413 7e040413
  //   2040383 2041503 2042583 413 b41413 140413 b41413 7c040413 4040383 4041503 4042583 413 b41413 140413
  //   b41413 78040413 8040383 8041503 8042583 413 b41413 140413 b41413 70040413 10040383 10041503 10042583
  //   413 b41413 140413 b41413 60040413 20040383 20041503 20042583 413 b41413 140413 b41413 40040413
  //   40040383 40041503 40042583 413 b41413 140413 b41413 140413 7ff40383 7ff41503 7ff42583 413 b41413
  //   240413 b41413 140413 fff40383 fff41503 fff42583 413 b41413 240413 b41413 240413 ffe40383 ffe41503
  //   ffe42583 413 b41413 240413 b41413 1040413 ff040383 ff041503 ff042583 413 b41413 240413 b41413
  //   2040413 fe040383 fe041503 fe042583 413 b41413 240413 b41413 40040413 c0040383 c0041503 c0042583 413
  //   b41413 340413 b41413 80040383 80041503 80042583
  //   Instruction Memory
  //   Halts Execution After Constant # of Clock Cycles
  //   Constant
endmodule
