// Logisim project m08_sb_immediate_bits.circ as structural Verilog: 1 circuit, main circuit run_main
module run_main (
  output [31:0] ra,
  output [31:0] sp,
  output [31:0] t0,
  output [31:0] t1,
  output [31:0] t2,
  output [31:0] s0,
  output [31:0] s1,
  output [31:0] a0,
  output [31:0] RequestedAddress,
  output [31:0] RequestedInstruction,
  output [15:0] TimeStep,
  output halt
);

  wire clk;

  Clock clock_1 (.out(clk));
  // Probe on RequestedAddress
  // cpu_harness cpu_harness_1: pin names not known; wires that end beside it: RequestedInstruction, clk, RequestedAddress, ra, sp, t0, t1, t2, s0, s1, a0
  ROM #(.addrWidth(14), .dataWidth(32)) rom_1 (.addr(RequestedAddress[15:2]), .data(RequestedInstruction));
  // Probe on RequestedInstruction
  Counter #(.max('hffff), .width(16)) counter_1 (.clk(clk), .Q(TimeStep));  // open: clr, load, up, count, D, carry
  Comparator #(.width(16)) comparator_1 (.a(TimeStep), .b(16'h16b), .eq(halt));  // open: gt, lt

  // Other names for the same wires on the sheet: Instruction[31:0] = RequestedInstruction;
  //   ProgramCounter[31:0] = RequestedAddress

  // Notes on the sheet:
  //   contents of rom_1 (hex, n*v repeats v):
  //   293 b29293 228293 b29293 413 b41413 240413 b41413 4400313 b31313 44630313 b31313 34430313 62a023
  //   28600313 b31313 65030313 b31313 640023 2a383 413 b41413 140413 b41413 7ff40413 4400313 b31313
  //   44630313 b31313 34430313 62a023 28600313 b31313 65030313 b31313 130313 6400a3 2a383 413 b41413
  //   140413 b41413 7fe40413 4400313 b31313 44630313 b31313 34430313 62a023 28600313 b31313 65030313
  //   b31313 230313 640123 2a383 413 b41413 140413 b41413 7fc40413 4400313 b31313 44630313 b31313 34430313
  //   62a023 28600313 b31313 65030313 b31313 330313 640223 2a383 413 b41413 140413 b41413 7f840413 4400313
  //   b31313 44630313 b31313 34430313 62a023 28600313 b31313 65030313 b31313 430313 640423 2a383 413
  //   b41413 140413 b41413 7f040413 4400313 b31313 44630313 b31313 34430313 62a023 28600313 b31313
  //   65030313 b31313 530313 640823 2a383 413 b41413 140413 b41413 7e140413 4400313 b31313 44630313 b31313
  //   34430313 62a023 28600313 b31313 65030313 b31313 630313 640fa3 2a383 413 b41413 140413 b41413
  //   7e040413 4400313 b31313 44630313 b31313 34430313 62a023 28600313 b31313 65030313 b31313 730313
  //   2640023 2a383 413 b41413 140413 b41413 7c040413 4400313 b31313 44630313 b31313 34430313 62a023
  //   28600313 b31313 65030313 b31313 830313 4640023 2a383 413 b41413 140413 b41413 78040413 4400313
  //   b31313 44630313 b31313 34430313 62a023 28600313 b31313 65030313 b31313 930313 8640023 2a383 413
  //   b41413 140413 b41413 70040413 4400313 b31313 44630313 b31313 34430313 62a023 28600313 b31313
  //   65030313 b31313 a30313 10640023 2a383 413 b41413 140413 b41413 60040413 4400313 b31313 44630313
  //   b31313 34430313 62a023 28600313 b31313 65030313 b31313 b30313 20640023 2a383 413 b41413 140413
  //   b41413 40040413 4400313 b31313 44630313 b31313 34430313 62a023 28600313 b31313 65030313 b31313
  //   c30313 40640023 2a383 413 b41413 140413 b41413 140413 4400313 b31313 44630313 b31313 34430313 62a023
  //   28600313 b31313 65030313 b31313 d30313 7e640fa3 2a383 413 b41413 240413 b41413 140413 4400313 b31313
  //   44630313 b31313 34430313 62a023 28600313 b31313 65030313 b31313 e30313 fe640fa3 2a383 413 b41413
  //   240413 b41413 240413 4400313 b31313 44630313 b31313 34430313 62a023 28600313 b31313 65030313 b31313
  //   f30313 fe640f23 2a383 413 b41413 240413 b41413 1040413 4400313 b31313 44630313 b31313 34430313
  //   62a023 28600313 b31313 65030313 b31313 1030313 fe640823 2a383 413 b41413 240413 b41413 2040413
  //   4400313 b31313 44630313 b31313 34430313 62a023 28600313 b31313 65030313 b31313 1130313 fe640023
  //   2a383 413 b41413 240413 b41413 40040413 4400313 b31313 44630313 b31313 34430313 62a023 28600313
  //   b31313 65030313 b31313 1230313 c0640023 2a383 413 b41413 340413 b41413 4400313 b31313 44630313
  //   b31313 34430313 62a023 28600313 b31313 65030313 b31313 1330313 80640023 2a383
  //   Instruction Memory
  //   Halts Execution After Constant # of Clock Cycles
  //   Constant
endmodule
