// Logisim project m09_effective_address_lanes.circ as structural Verilog: 1 circuit, main circuit run_main
module run_main (
  output [31:0] ra,
  output [31:0] sp,
  output [31:0] t0,
  output [31:0] t1,
  output [31:0] t2,
  output [31:0] s0,
  output [31:0] s1,
  output [31:0] a0,
  output [31:0] RequestedAddress,
  output [31:0] RequestedInstruction,
  output [15:0] TimeStep,
  output halt
);

  wire clk;

  Clock clock_1 (.out(clk));
  // Probe on RequestedAddress
  // cpu_harness cpu_harness_1: pin names not known; wires that end beside it: RequestedInstruction, clk, RequestedAddress, ra, sp, t0, t1, t2, s0, s1, a0
  ROM #(.addrWidth(14), .dataWidth(32)) rom_1 (.addr(RequestedAddress[15:2]), .data(RequestedInstruction));
  // Probe on RequestedInstruction
  Counter #(.max('hffff), .width(16)) counter_1 (.clk(clk), .Q(TimeStep));  // open: clr, load, up, count, D, carry
  Comparator #(.width(16)) comparator_1 (.a(TimeStep), .b(16'h6d), .eq(halt));  // open: gt, lt

  // Other names for the same wires on the sheet: Instruction[31:0] = RequestedInstruction;
  //   ProgramCounter[31:0] = RequestedAddress

  // Notes on the sheet:
  //   contents of rom_1 (hex, n*v repeats v):
  //   40000293 20300313 b31313 7ef30313 b31313 70130313 62a023 4800313 b31313 68a30313 b31313 67830313
  //   62a223 40100413 40383 40100413 140383 40100413 240383 40300413 ffd40383 40300413 ffe40383 40300413
  //   fff40383 3ff00413 140383 3ff00413 240383 3ff00413 340383 3ff00413 440383 3ff00413 142383 40100413
  //   141383 4400313 b31313 44630313 b31313 34430313 62a023 40100413 2aa00313 b31313 77930313 b31313
  //   48030313 640023 2a383 4400313 b31313 44630313 b31313 34430313 62a023 3ff00413 2aa00313 b31313
  //   77930313 b31313 48030313 6401a3 2a383 4400313 b31313 44630313 b31313 34430313 62a023 40300413
  //   2aa00313 b31313 77930313 b31313 48030313 fe640ea3 2a383 4400313 b31313 44630313 b31313 34430313
  //   62a023 40100413 2aa00313 b31313 77930313 b31313 48030313 640123 2a383 4400313 b31313 44630313 b31313
  //   34430313 62a023 3ff00413 37a00313 b31313 5b730313 b31313 6ef30313 6411a3 2a383
  //   Instruction Memory
  //   Halts Execution After Constant # of Clock Cycles
  //   Constant
endmodule
