// Logisim project m10_store_register_protection.circ as structural Verilog: 1 circuit, main circuit run_main
module run_main (
  output [31:0] ra,
  output [31:0] sp,
  output [31:0] t0,
  output [31:0] t1,
  output [31:0] t2,
  output [31:0] s0,
  output [31:0] s1,
  output [31:0] a0,
  output [31:0] RequestedAddress,
  output [31:0] RequestedInstruction,
  output [15:0] TimeStep,
  output halt
);

  wire clk;

  Clock clock_1 (.out(clk));
  // Probe on RequestedAddress
  // cpu_harness cpu_harness_1: pin names not known; wires that end beside it: RequestedInstruction, clk, RequestedAddress, ra, sp, t0, t1, t2, s0, s1, a0
  ROM #(.addrWidth(14), .dataWidth(32)) rom_1 (.addr(RequestedAddress[15:2]), .data(RequestedInstruction));
  // Probe on RequestedInstruction
  Counter #(.max('hffff), .width(16)) counter_1 (.clk(clk), .Q(TimeStep));  // open: clr, load, up, count, D, carry
  Comparator #(.width(16)) comparator_1 (.a(TimeStep), .b(16'h55), .eq(halt));  // open: gt, lt

  // Other names for the same wires on the sheet: Instruction[31:0] = RequestedInstruction;
  //   ProgramCounter[31:0] = RequestedAddress

  // Notes on the sheet:
  //   contents of rom_1 (hex, n*v repeats v):
  //   40000a13 4800a93 ba9a93 690a8a93 ba9a93 ffa8a93 a2023 30a00093 15a00a3 8393 a2503 a2223 30e00293
  //   15a02a3 28393 4a2503 a2223 31000393 15a03a3 38393 4a2503 a2423 31100413 15a0423 40393 8a2503 a2623
  //   31500613 15a0623 60393 ca2503 a2e23 32800f93 15a0fa3 f8393 1ca2503 a2023 30b00113 15a1123 10393
  //   a2503 a2223 30f00313 15a1323 30393 4a2503 a2423 31100413 15a1423 40393 8a2503 a2623 31500613 15a1623
  //   60393 ca2503 a2e23 32700f13 15a1f23 f0393 1ca2503 a2223 30d00213 15a2223 20393 4a2503 a2423 31100413
  //   15a2423 40393 8a2503 a2623 31500613 15a2623 60393 ca2503 a2e23 32500e13 15a2e23 e0393 1ca2503 a0413
  //   a8493
  //   Instruction Memory
  //   Halts Execution After Constant # of Clock Cycles
  //   Constant
endmodule
