// Logisim project m11_zero_and_dependencies.circ as structural Verilog: 1 circuit, main circuit run_main
module run_main (
  output [31:0] ra,
  output [31:0] sp,
  output [31:0] t0,
  output [31:0] t1,
  output [31:0] t2,
  output [31:0] s0,
  output [31:0] s1,
  output [31:0] a0,
  output [31:0] RequestedAddress,
  output [31:0] RequestedInstruction,
  output [15:0] TimeStep,
  output halt
);

  wire clk;

  Clock clock_1 (.out(clk));
  // Probe on RequestedAddress
  // cpu_harness cpu_harness_1: pin names not known; wires that end beside it: RequestedInstruction, clk, RequestedAddress, ra, sp, t0, t1, t2, s0, s1, a0
  ROM #(.addrWidth(14), .dataWidth(32)) rom_1 (.addr(RequestedAddress[15:2]), .data(RequestedInstruction));
  // Probe on RequestedInstruction
  Counter #(.max('hffff), .width(16)) counter_1 (.clk(clk), .Q(TimeStep));  // open: clr, load, up, count, D, carry
  Comparator #(.width(16)) comparator_1 (.a(TimeStep), .b(16'h2d), .eq(halt));  // open: gt, lt

  // Other names for the same wires on the sheet: Instruction[31:0] = RequestedInstruction;
  //   ProgramCounter[31:0] = RequestedAddress

  // Notes on the sheet:
  //   contents of rom_1 (hex, n*v repeats v):
  //   40000293 20300313 b31313 7ef30313 b31313 70130313 62a023 313 62a223 28003 393 2a403 29003 393 2a403
  //   2a003 393 2a403 fff00313 62a023 280a3 2a383 fff00313 62a023 29123 2a383 fff00313 62a023 2a023 2a383
  //   20000313 b31313 b31313 130313 62a023 2a303 130393 72a223 42a403 328303 6304b3 928223 42a503
  //   Instruction Memory
  //   Halts Execution After Constant # of Clock Cycles
  //   Constant
endmodule
