// Logisim project r12_mulhu.circ as structural Verilog: 1 circuit, main circuit run_main
module run_main (
  output [31:0] ra,
  output [31:0] sp,
  output [31:0] t0,
  output [31:0] t1,
  output [31:0] t2,
  output [31:0] s0,
  output [31:0] s1,
  output [31:0] a0,
  output [31:0] RequestedAddress,
  output [31:0] RequestedInstruction,
  output [15:0] TimeStep,
  output halt
);

  wire clk;

  Clock clock_1 (.out(clk));
  // Probe on RequestedAddress
  // cpu_harness cpu_harness_1: pin names not known; wires that end beside it: RequestedInstruction, clk, RequestedAddress, ra, sp, t0, t1, t2, s0, s1, a0
  ROM #(.addrWidth(14), .dataWidth(32)) rom_1 (.addr(RequestedAddress[15:2]), .data(RequestedInstruction));
  // Probe on RequestedInstruction
  Counter #(.max('hffff), .width(16)) counter_1 (.clk(clk), .Q(TimeStep));  // open: clr, load, up, count, D, carry
  Comparator #(.width(16)) comparator_1 (.a(TimeStep), .b(16'h5f), .eq(halt));  // open: gt, lt

  // Other names for the same wires on the sheet: Instruction[31:0] = RequestedInstruction;
  //   ProgramCounter[31:0] = RequestedAddress

  // Notes on the sheet:
  //   contents of rom_1 (hex, n*v repeats v):
  //   293 21d00313 b31313 4a830313 b31313 32130313 262b3b3 100293 21d00313 b31313 4a830313 b31313 32130313
  //   262b3b3 700293 900313 262b3b3 ff900293 900313 262b3b3 700293 ff700313 262b3b3 ff900293 ff700313
  //   262b3b3 fff00293 fff00313 262b3b3 fff00293 200313 262b3b3 200293 fff00313 262b3b3 293 b29293 2028293
  //   b29293 313 b31313 2030313 b31313 262b3b3 1ff00293 b29293 7ff28293 b29293 7ff28293 1ff00313 b31313
  //   7ff30313 b31313 7ff30313 262b3b3 20000293 b29293 b29293 fff00313 262b3b3 20000293 b29293 b29293
  //   200313 262b3b3 20000293 b29293 b29293 20000313 b31313 b31313 262b3b3 4800293 b29293 68a28293 b29293
  //   67828293 26a00313 b31313 79b30313 b31313 6f030313 262b3b3 ff900293 300313 262b2b3 28413 ff900293
  //   300313 262b333 30413 ffd00293 252b3b3
  //   Instruction Memory
  //   Halts Execution After Constant # of Clock Cycles
  //   Constant
endmodule
