// Logisim project r14_zero_and_register_ports.circ as structural Verilog: 1 circuit, main circuit run_main
module run_main (
  output [31:0] ra,
  output [31:0] sp,
  output [31:0] t0,
  output [31:0] t1,
  output [31:0] t2,
  output [31:0] s0,
  output [31:0] s1,
  output [31:0] a0,
  output [31:0] RequestedAddress,
  output [31:0] RequestedInstruction,
  output [15:0] TimeStep,
  output halt
);

  wire clk;

  Clock clock_1 (.out(clk));
  // Probe on RequestedAddress
  // cpu_harness cpu_harness_1: pin names not known; wires that end beside it: RequestedInstruction, clk, RequestedAddress, ra, sp, t0, t1, t2, s0, s1, a0
  ROM #(.addrWidth(14), .dataWidth(32)) rom_1 (.addr(RequestedAddress[15:2]), .data(RequestedInstruction));
  // Probe on RequestedInstruction
  Counter #(.max('hffff), .width(16)) counter_1 (.clk(clk), .Q(TimeStep));  // open: clr, load, up, count, D, carry
  Comparator #(.width(16)) comparator_1 (.a(TimeStep), .b(16'h61), .eq(halt));  // open: gt, lt

  // Other names for the same wires on the sheet: Instruction[31:0] = RequestedInstruction;
  //   ProgramCounter[31:0] = RequestedAddress

  // Notes on the sheet:
  //   contents of rom_1 (hex, n*v repeats v):
  //   ff900293 300313 628033 393 ff900293 300313 40628033 393 ff900293 300313 62f033 393 ff900293 300313
  //   62e033 393 ff900293 300313 62c033 393 ff900293 300313 629033 393 ff900293 300313 62d033 393 ff900293
  //   300313 4062d033 393 100293 200313 62a033 393 ff900293 300313 2628033 393 fff00293 200313 2629033 393
  //   fff00293 200313 262b033 393 ff900293 500333 283b3 40500333 400283b3 507333 2f3b3 506333 2e3b3 504333
  //   2c3b3 501333 293b3 505333 2d3b3 40505333 4002d3b3 502333 2a3b3 2500333 20283b3 2501333 20293b3
  //   2503333 202b3b3 b00093 1600113 2c00213 5800413 a000813 13600f93 41f083b3 401f83b3 41f103b3 402f83b3
  //   41f203b3 404f83b3 41f403b3 408f83b3 41f803b3 410f83b3 41ff83b3 41ff83b3 410f8f33 f0393 401f03b3
  //   41e083b3
  //   Instruction Memory
  //   Halts Execution After Constant # of Clock Cycles
  //   Constant
endmodule
